# Fritzing sketch Pi-BQ with adafruit Cobbler Plus (saved by Fritzing 0.9.3b)
breadboards: 1

parts:
  Raspberry_Pi_1 = Raspberry Pi 3 [part_number=RPI-3-V1.2]  # not connected
  BREAKOUT1 = MAX31850 Thermocouple Breakout
  BREAKOUT2 = MAX31850 Thermocouple Breakout
  R1 = Resistor [tolerance=±5% resistance=4.7k package="0603 [SMD]"]
  Part1 = Adafruit Pi Cobbler Plus [part_number="Adafruit #2029"]

nets:
  GND: BREAKOUT1.GND, BREAKOUT2.GND, Part1.GND
  VIN: BREAKOUT1.VIN, BREAKOUT2.VIN, R1.Pin_1, Part1.+3.3V
  N1: BREAKOUT1.DATA, BREAKOUT2.DATA, R1.Pin_0, Part1.GPIO4

custom parts:
  Adafruit Pi Cobbler Plus: The Raspberry Pi B+/Pi 2/ Pi 3 has landed on the Maker World like a 40-GPIO pinned, quad-USB ported, credit card sized bomb of DIY joy. And while you can use most of our great Model B accessories by hooking up our downgrade cable, its probably a good time to upgrade your set up and accessorize using all of the Model B+'s / Pi 2's / Pi 3's 40 pins. That's why we now carry the Adafruit Assembled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
